# Fritzing sketch project 2 (saved by Fritzing 0.9.3b)
breadboards: 2

parts:
  YwRobot_Power_Supply1 = YwRobot Breadboard Power Supply [part_number=545043]
  U2 = NodeMCU V1.0
  R1 = Photocell (LDR) [package=THT]  # not connected
  R2 = Resistor [tolerance=±5% resistance=220 package="0805 [SMD]"]
  BAT1 = BC9VPC [package=bc9vpc]  # not connected
  hc-sr1 = hc-sr04
  J1 = Basic Servo  # not connected
  J2 = Basic Servo
  D1 = LTE-302 [package=lte-302]
  R3 = Resistor [tolerance=±5% resistance=220 package="0805 [SMD]"]
  LED1 = RGB LED (com. cathode, rbg) [package="5 mm [THT]"]
  R4 = Resistor [tolerance=±5% resistance=220 package="0805 [SMD]"]

nets:
  VCC: YwRobot_Power_Supply1.VCC#5, hc-sr1.VCC, J2.vcc
  N1: YwRobot_Power_Supply1.VCC#9, U2.Vin, R2.Pin_0, D1.C
  GND: YwRobot_Power_Supply1.GND#11, hc-sr1.GND, J2.gnd
  N2: YwRobot_Power_Supply1.GND#13, R2.Pin_1, R3.Pin_1, R4.Pin_1
  N3: U2.D1, hc-sr1.Echo
  N4: U2.D2, hc-sr1.Trig
  N5: U2.D5, LED1.red_anode
  N6: U2.D6, LED1.common_cathode
  N7: U2.D7, LED1.green_anode
  N8: D1.A, R3.Pin_0
  N9: LED1.blue_anode, R4.Pin_0

notes:
  3,3V
  5V

custom parts:
  YwRobot Breadboard Power Supply: The YwRobot Breadboard Power Supply (MB-V2) has two power rails; they can be 5V or 3V3. Power to the module can be provided through the female USB socket or through the A10 (female) 2.1mm power jack.
  NodeMCU V1.0: ESP8266 based NodeMCU
