# Fritzing sketch Project 3 (saved by Fritzing 0.9.3b)
breadboards: 1

parts:
  Onderdeel1 = Arduino Uno (Rev3) - ICSP
  Onderdeel2 = RFID-RC522-v3
  Matrix_keypad1 = KEYPAD 4x4

nets:
  N1: Onderdeel1.A0, Matrix_keypad1.row1
  N2: Onderdeel1.A1, Matrix_keypad1.row2
  N3: Onderdeel1.A2, Matrix_keypad1.row3
  N4: Onderdeel1.A3, Matrix_keypad1.row4
  N5: Onderdeel1.ICSP_MISO, Onderdeel1.D12/MISO, Onderdeel2.SCK
  N6: Onderdeel1.D9_PWM, Onderdeel2.RST
  N7: Onderdeel1.D10_PWM/SS, Onderdeel2.MISO
  N8: Onderdeel1.D11_PWM/MOSI, Onderdeel2.MOSI
  N9: Onderdeel1.D13/SCK, Onderdeel2.SDA
  GND: Onderdeel1.GND, Onderdeel2.GND
  N10: Onderdeel1.D2, Matrix_keypad1.col4
  N11: Onderdeel1.D3_PWM, Matrix_keypad1.col3
  N12: Onderdeel1.D4, Matrix_keypad1.col2
  N13: Onderdeel1.D5_PWM, Matrix_keypad1.col1
  3V3: Onderdeel1.3V3, Onderdeel2.3.3V

custom parts:
  RFID-RC522-v3: A simple China made RFID-RC522 Reader (6x4 cm); do check the pin labels, as this is a MFRC522 based clone.
  KEYPAD 4x4: Matrix keypad 16 buttons, 4 rows x 4 columns
