# Fritzing sketch Dotmatrix (saved by Fritzing 0.9.3b)

parts:
  Onderdeel1 = Arduino Uno (Rev3) - ICSP
  Disp1 = LBT2088AH [part_number=LBT2088AH]

nets:
  N1: Onderdeel1.A2, Disp1.pin_5
  N2: Onderdeel1.A3, Disp1.pin_6
  N3: Onderdeel1.A4/SDA, Disp1.pin_7
  N4: Onderdeel1.A5/SCL, Disp1.pin_8
  N5: Onderdeel1.ICSP_MISO, Onderdeel1.D12/MISO, Disp1.pin2
  N6: Onderdeel1.D8, Disp1.pin_15
  N7: Onderdeel1.D9_PWM, Disp1.pin_16
  N8: Onderdeel1.D10_PWM/SS, Disp1.pin_4
  N9: Onderdeel1.D11_PWM/MOSI, Disp1.pin_3
  N10: Onderdeel1.D13/SCK, Disp1.pin1
  N11: Onderdeel1.D2, Disp1.pin_9
  N12: Onderdeel1.D3_PWM, Disp1.pin_10
  N13: Onderdeel1.D4, Disp1.pin_11
  N14: Onderdeel1.D5_PWM, Disp1.pin_12
  N15: Onderdeel1.D6_PWM, Disp1.pin_13
  N16: Onderdeel1.D7, Disp1.pin_14
